# Fritzing sketch Sniffer (saved by Fritzing 0.9.2b)
breadboards: 1

parts:
  R1 = Resistor [tolerance=±5% resistance=220 package="2512 [SMD]"]
  LED1 = DUO LED RG [package="5 mm [THT]"]
  U2 = atmega328 [package=dip]
  XTAL2 = Crystal [frequency="16 Mhz" package=THT]
  R3 = Resistor [tolerance=±5% resistance=10k package=THT]
  C5 = Ceramic Capacitor [capacitance=22pF voltage=50V package="100 mil [THT, multilayer]"]
  C6 = Ceramic Capacitor [capacitance=22pF voltage=50V package="100 mil [THT, multilayer]"]
  C4 = Electrolytic Capacitor [capacitance=1µF package="100 mil [THT, electrolytic]"]
  DHT1 = DHT11 Humitidy and Temperature Sensor
  R4 = Resistor [tolerance=±5% resistance=10k package=THT]

nets:
  N1: R1.Pin_0, LED1.common_cathode
  N2: LED1.red_anode, U2.D3_(PWM)
  N3: LED1.green_anode, U2.D4
  N4: U2.RESET, R3.Pin_0
  VCC: U2.VCC, R3.Pin_1, DHT1.VDD
  N5: U2.GND#7, C5.1, C6.0, DHT1.GND, R4.Pin_1
  N6: U2.XLAT1, XTAL2.pin_1, C5.0
  N7: U2.XLAT2, XTAL2.pin_0, C6.1
  N8: U2.D5_(PWM), DHT1.DATA, R4.Pin_0
  N9: U2.AVCC, U2.AREF, C4.+
  N10: U2.GND#21, C4.-

notes:
  5V
  GND

custom parts:
  DHT11 Humitidy and Temperature Sensor: DHT11 Humidity and Temperature Sensor
